# Fritzing sketch MCP3008_F303K8_Test (saved by Fritzing 0.9.3b)
breadboards: 2
perfboards: 2

parts:
  IC1 = IC, DIP package, 16 pins [chip_label=MCP3208]
  IC2 = IC, DIP package, 16 pins [chip_label=MCP3208]
  C1 = Ceramic Capacitor [capacitance=100nF package="100 mil [THT, multilayer]"]
  C2 = Ceramic Capacitor [capacitance=100nF package="100 mil [THT, multilayer]"]
  R1 = Rotary Potentiometer (Small) [maximum_resistance=100kΩ package=THT]  # not connected
  R2 = Rotary Potentiometer (Small) [maximum_resistance=100kΩ package=THT]  # not connected
  R3 = Rotary Potentiometer (Small) [maximum_resistance=100kΩ package=THT]  # not connected
  R4 = Rotary Potentiometer (Small) [maximum_resistance=100kΩ package=THT]  # not connected
  U1 = mystery part, 30 pins [chip_label="Nucleo F303"]
  R5 = Resistor [tolerance=±5% resistance=33 package=THT]
  R6 = Resistor [tolerance=±5% resistance=33 package=THT]

nets:
  N1: IC1.pin9, IC1.pin14, IC2.pin4, IC2.pin5, IC2.pin6, IC2.pin7, IC2.pin8, IC2.pin9, IC2.pin14, C1.1, C2.1, U1.pin14
  N2: IC1.pin10, U1.pin28
  N3: IC1.pin11, IC2.pin11, R5.Pin_0
  N4: IC1.pin12, IC2.pin12, U1.pin30
  N5: IC1.pin13, IC2.pin13, R6.Pin_0
  N6: IC1.pin15, IC1.pin16, IC2.pin15, IC2.pin16, C1.0, C2.0, U1.pin12
  N7: IC2.pin10, U1.pin27
  N8: U1.pin1, R6.Pin_1
  N9: U1.pin29, R5.Pin_1

notes:
  POT x 8
  POT x 3
  GND
  +5V
