# Fritzing sketch MCP3008_SimpleTest (saved by Fritzing 0.9.3b)
breadboards: 1

parts:
  IC1 = IC, DIP package, 16 pins [chip_label=MCP3208]
  C1 = Ceramic Capacitor [capacitance=100nF package="100 mil [THT, multilayer]"]
  J1 = STM32 Nucleo boards
  R1 = Rotary Potentiometer (Small) [maximum_resistance=100kΩ package=THT]

nets:
  N1: IC1.pin1, R1.wiper
  N2: IC1.pin2, IC1.pin3, IC1.pin4, IC1.pin5, IC1.pin6, IC1.pin7, IC1.pin8, IC1.pin9, IC1.pin14, C1.1, J1.GND, R1.leg1
  N3: IC1.pin10, J1.D10_PWM/SS
  N4: IC1.pin11, J1.D11_PWM/MOSI
  N5: IC1.pin12, J1.D12/MISO
  N6: IC1.pin13, J1.D13/SCK
  N7: IC1.pin15, IC1.pin16, C1.0, J1.5V, R1.leg2

notes:
  GND
  +5V or +3.3V
  10kΩ
