# Fritzing sketch MCP3208_Test (saved by Fritzing 0.9.3b)
breadboards: 1
perfboards: 2

parts:
  IC1 = IC, DIP package, 16 pins [chip_label=MCP3208]
  IC2 = IC, DIP package, 16 pins [chip_label=MCP3208]
  C1 = Ceramic Capacitor [capacitance=100nF package="100 mil [THT, multilayer]"]
  C2 = Ceramic Capacitor [capacitance=100nF package="100 mil [THT, multilayer]"]
  J1 = STM32 Nucleo boards
  R1 = Rotary Potentiometer (Small) [maximum_resistance=100kΩ package=THT]  # not connected
  R2 = Rotary Potentiometer (Small) [maximum_resistance=100kΩ package=THT]  # not connected
  R3 = Rotary Potentiometer (Small) [maximum_resistance=100kΩ package=THT]  # not connected
  R4 = Rotary Potentiometer (Small) [maximum_resistance=100kΩ package=THT]  # not connected

nets:
  N1: IC1.pin9, IC1.pin14, IC2.pin4, IC2.pin5, IC2.pin6, IC2.pin7, IC2.pin8, IC2.pin9, IC2.pin14, C1.1, C2.1, J1.GND
  N2: IC1.pin10, J1.D10_PWM/SS
  N3: IC1.pin11, IC2.pin11, J1.D11_PWM/MOSI
  N4: IC1.pin12, IC2.pin12, J1.D12/MISO
  N5: IC1.pin13, IC2.pin13, J1.D13/SCK
  N6: IC1.pin15, IC1.pin16, IC2.pin15, IC2.pin16, C1.0, C2.0, J1.5V
  N7: IC2.pin10, J1.D9_PWM

notes:
  POT x 8
  POT x 3
